// Logisim project alu.circ as structural Verilog: 1 circuit, main circuit alu
module alu (
  input  [31:0] A,
  input  [31:0] B,
  input  [3:0] ALUSel,
  output [31:0] ALUResult
);

  wire comparator_1_lt;
  wire [4:0] bit_extender_2_out, bit_extender_3_out, bit_extender_4_out;
  wire [31:0] adder_1_out, and7, bit_extender_1_out, multiplier_1_cout, multiplier_1_out, multiplier_2_cout,
       or6, shifter_2_out, shifter_3_out, sll1, subtractor_1_out, xor4;

  Comparator #(.width(32)) comparator_1 (.a(A), .b(B), .lt(comparator_1_lt));  // open: gt, eq
  assign bit_extender_1_out = {{31{1'b0}}, comparator_1_lt};  // Bit_Extender bit_extender_1
  Bit_Extender #(.in_width(32), .out_width(5)) bit_extender_2 (.in(B), .out(bit_extender_2_out));
  Adder #(.width(32)) adder_1 (.a(B), .b(A), .out(adder_1_out));  // open: cin, cout
  Shifter #(.width(32)) shifter_1 (.in(A), .\dist (bit_extender_2_out), .out(sll1));
  assign xor4 = A ^ B;  // XOR_Gate xor_1, 32 bits wide
  assign or6 = A | B;  // OR_Gate or_1, 32 bits wide
  assign and7 = A & B;  // AND_Gate and_1, 32 bits wide
  Multiplier #(.mode("twosComplement"), .width(32)) multiplier_1 (
    .a(A), .b(B), .out(multiplier_1_out), .cout(multiplier_1_cout));  // open: cin
  Multiplier #(.width(32)) multiplier_2 (.a(A), .b(B), .cout(multiplier_2_cout));  // open: out, cin
  Subtractor #(.width(32)) subtractor_1 (.a(A), .b(B), .out(subtractor_1_out));  // open: bin, bout
  Shifter #(.shift("lr"), .width(32)) shifter_2 (.in(A), .\dist (bit_extender_3_out), .out(shifter_2_out));
  Bit_Extender #(.in_width(32), .out_width(5), .\type ("zero")) bit_extender_3 (.in(B), .out(bit_extender_3_out));
  Multiplexer #(.select(4), .width(32)) multiplexer_1 (
    .in0(adder_1_out), .in1(sll1), .in2(bit_extender_1_out), .in4(xor4), .in5(shifter_2_out), .in6(or6),
    .in7(and7), .in8(multiplier_1_out), .in9(multiplier_1_cout), .in11(multiplier_2_cout),
    .in12(subtractor_1_out), .in13(shifter_3_out), .in15(B), .out(ALUResult), .sel(ALUSel));  // open: in3, in10, in14
  Bit_Extender #(.in_width(32), .out_width(5)) bit_extender_4 (.in(B), .out(bit_extender_4_out));
  Shifter #(.shift("ar"), .width(32)) shifter_3 (.in(A), .\dist (bit_extender_4_out), .out(shifter_3_out));

  // Notes on the sheet:
  //   INPUTS to your circuit
  //   DON'T CHANGE THE LOCATIONS OF THE INPUTS AND OUTPUTS!
  //   OUTPUT from your circuit
endmodule
