// Logisim project control-logic.circ as structural Verilog: 1 circuit, main circuit control_logic
module control_logic (
  input  [31:0] Instruction,
  input  BrEq,
  input  BrLt,
  output PCSel,
  output RegWEn,
  output [2:0] ImmSel,
  output BrUn,
  output ASel,
  output BSel,
  output [3:0] ALUSel,
  output MemRW,
  output [1:0] WBSel
);

  wire and_2_out, and_3_out, and_4_out, and_5_out, and_6_out, and_7_out, auipc, bdet, comparator_2_eq,
       comparator_3_eq, comparator_4_eq, comparator_5_eq, comparator_6_eq, comparator_7_eq, comparator_10_eq,
       comparator_11_eq, comparator_12_eq, fourthing, Itype13, jal, jalr, lui, not_1_out, not_2_out,
       not_3_out, not_4_out, or_1_out, or_3_out, or_4_out, or_5_out, or_7_out, or_9_out, or_13_out, Rtype,
       zerothree;
  wire [1:0] WBSell;
  wire [2:0] ImmSell;
  wire [3:0] multiplexer_1_out, multiplexer_2_out, multiplexer_3_out, multiplexer_4_out, multiplexer_5_out;
  wire [15:0] rom_1_data;

  Multiplexer #(.width(4)) multiplexer_1 (.in0(4'b0101), .in1(4'b1101), .out(multiplexer_1_out), .sel(Instruction[30]));
  Comparator #(.width(7)) comparator_1 (.a(Instruction[6:0]), .b(7'b1100011), .eq(bdet));  // open: gt, lt
  ROM #(.addrWidth(6), .dataWidth(16)) rom_1 (.data(rom_1_data));  // open: addr
  Multiplexer #(.select(2), .width(4)) multiplexer_2 (
    .in0(4'b0000), .in1(4'b0000), .in2(4'b0000), .in3(4'b0000), .out(multiplexer_2_out),
    .sel({Instruction[30], Instruction[25]}));
  Comparator #(.width(3)) comparator_2 (.a(Instruction[14:12]), .b(3'b000), .eq(comparator_2_eq));  // open: gt, lt
  Comparator #(.width(3)) comparator_3 (.a(Instruction[14:12]), .b(3'b001), .eq(comparator_3_eq));  // open: gt, lt
  Comparator #(.width(3)) comparator_4 (.a(Instruction[14:12]), .b(3'b100), .eq(comparator_4_eq));  // open: gt, lt
  Comparator #(.width(3)) comparator_5 (.a(Instruction[14:12]), .b(3'b101), .eq(comparator_5_eq));  // open: gt, lt
  Comparator #(.width(3)) comparator_6 (.a(Instruction[14:12]), .b(3'b110), .eq(comparator_6_eq));  // open: gt, lt
  Comparator #(.width(3)) comparator_7 (.a(Instruction[14:12]), .b(3'b111), .eq(comparator_7_eq));  // open: gt, lt
  Multiplexer #(.select(3), .width(4)) multiplexer_3 (
    .in0(4'b0000), .in1(4'b0001), .in2(4'b0010), .in3(4'b0000), .in4(4'b0100), .in5(multiplexer_1_out),
    .in6(4'b0110), .in7(4'b0111), .out(multiplexer_3_out), .sel(Instruction[14:12]));
  or or_1 (or_1_out, comparator_6_eq, comparator_7_eq);
  Comparator #(.width(7)) comparator_8 (.a(Instruction[6:0]), .b(7'b0100011), .eq(MemRW));  // open: gt, lt
  Comparator #(.width(7)) comparator_9 (.a(Instruction[6:0]), .b(7'b0010111), .eq(auipc));  // open: gt, lt
  Multiplexer #(.select(3), .width(4)) multiplexer_4 (
    .in0(multiplexer_2_out), .in1(4'b0001), .in2(4'b0010), .in3(4'b1011), .in4(4'b0100), .in5(4'b0101),
    .in6(4'b0110), .in7(4'b0111), .out(multiplexer_4_out), .sel(Instruction[14:12]));
  and and_1 (BrUn, bdet, or_1_out);
  Comparator #(.width(7)) comparator_10 (.a(Instruction[6:0]), .b(7'b0010111), .eq(comparator_10_eq));  // open: gt, lt
  Comparator #(.width(7)) comparator_11 (.a(Instruction[6:0]), .b(7'b1101111), .eq(comparator_11_eq));  // open: gt, lt
  Comparator #(.width(7)) comparator_12 (.a(Instruction[6:0]), .b(7'b0000011), .eq(comparator_12_eq));  // open: gt, lt
  Comparator #(.width(7)) comparator_13 (.a(Instruction[6:0]), .b(7'b0010011), .eq(Itype13));  // open: gt, lt
  Multiplexer #(.width(4)) multiplexer_5 (
    .in0(multiplexer_3_out), .in1(multiplexer_4_out), .out(multiplexer_5_out), .sel(Rtype));
  and and_2 (and_2_out, BrEq, bdet, comparator_2_eq);
  not not_1 (not_1_out, BrEq);
  not not_2 (not_2_out, BrLt);
  and and_3 (and_3_out, BrLt, bdet, comparator_6_eq);
  not not_3 (not_3_out, BrLt);
  or or_2 (ASel, bdet, comparator_10_eq, comparator_11_eq);
  Multiplexer #(.width(2)) multiplexer_6 (.in0(2'b00), .in1(2'b01), .out(WBSell), .sel(comparator_12_eq));
  and and_4 (and_4_out, bdet, comparator_3_eq, not_1_out);
  and and_5 (and_5_out, BrLt, comparator_4_eq, bdet);
  and and_6 (and_6_out, bdet, comparator_5_eq, not_2_out);
  and and_7 (and_7_out, comparator_7_eq, not_3_out, bdet);
  or or_3 (or_3_out, Itype13, zerothree, Rtype);
  Comparator #(.width(7)) comparator_14 (.a(Instruction[6:0]), .b(7'b0000011), .eq(zerothree));  // open: gt, lt
  Multiplexer #(.width(4)) multiplexer_7 (.in0(multiplexer_5_out), .in1(4'b1111), .out(ALUSel), .sel(lui));
  Comparator #(.width(7)) comparator_15 (.a(Instruction[6:0]), .b(7'b0110011), .eq(Rtype));  // open: gt, lt
  or or_4 (or_4_out, and_2_out, and_4_out, and_5_out, and_6_out, and_3_out, and_7_out);
  or or_5 (or_5_out, jalr, jal);
  or or_6 (RegWEn, or_3_out, fourthing);
  or or_7 (or_7_out, fourthing, not_4_out);
  not not_4 (not_4_out, Rtype);
  or or_8 (BSel, Itype13, bdet, zerothree, fourthing);
  or or_9 (or_9_out, jalr, jal);
  // OR_Gate or_10 has open pins: in0=2'b01, in1=2'b10, out=open
  Comparator #(.width(7)) comparator_16 (.a(Instruction[6:0]), .b(7'b1101111), .eq(jal));  // open: gt, lt
  Comparator #(.width(7)) comparator_17 (.a(Instruction[6:0]), .b(7'b1100111), .eq(jalr));  // open: gt, lt
  Multiplexer #(.width(2)) multiplexer_8 (.in0(WBSell), .in1(2'b10), .out(WBSel), .sel(or_5_out));
  or or_11 (PCSel, or_4_out, or_9_out);
  Comparator #(.width(7)) comparator_18 (.a(Instruction[6:0]), .b(7'b0110111), .eq(lui));  // open: gt, lt
  Multiplexer #(.width(3)) multiplexer_9 (.in0(3'b000), .in1(3'b010), .out(ImmSell), .sel(bdet));
  or or_12 (fourthing, lui, jal, jalr, auipc);
  or or_13 (or_13_out, lui, auipc);
  Multiplexer #(.width(3)) multiplexer_10 (.in0(ImmSell), .in1(3'b011), .out(ImmSel), .sel(or_13_out));

  // Other names for the same wires on the sheet: opcode[6:0] = Instruction[6:0]; funct3[2:0] = Instruction[14:12]

  // Notes on the sheet:
  //   INPUTS to your circuit
  //   Connect ROM Input here ->
  //   ROM FOR CONTROL LOGIC
  //   DON'T CHANGE THE LOCATIONS OF THE INPUTS AND OUTPUTS!
  //   This is only if you choose to do the ROM option
  //   CONNECT
  //   WIRE
  //   TO
  //   USE
  //   ROM
  //   OUTPUT from your circuit
  //   Reminder: If using ROM, use combinational logic for PCSel
endmodule
