// Logisim project cpu.circ as structural Verilog: 1 circuit, main circuit cpu
module cpu (
  input  clk,
  input  [31:0] Instruction,
  input  [31:0] MemReadData,
  output [31:0] MemAddress,
  output [31:0] ProgramCounter,
  output [31:0] ra,
  output [31:0] sp,
  output [31:0] t0,
  output [31:0] t1,
  output [31:0] t2,
  output [31:0] s0,
  output [31:0] s1,
  output [31:0] a0,
  output [3:0] MemWriteMask,
  output [31:0] MemWriteData
);

  wire branch_comp_1_breq, branch_comp_1_brlt, comparator_1_eq, control_logic_1_asel, control_logic_1_brun,
       control_logic_1_bsel, control_logic_1_memrw, control_logic_1_regwen, flush, JRSEL, or_1_out, PCSel;
  wire [1:0] control_logic_1_wbsel;
  wire [2:0] control_logic_1_immsel;
  wire [3:0] control_logic_1_alusel;
  wire [31:0] adder_2_out, i2, imm, multiplexer_1_out, multiplexer_2_out, multiplexer_3_out,
       multiplexer_4_out, multiplexer_5_out, partial_load_1_datatoreg, pc2, pcplusfour, regfile_1_readdata1,
       rs2, WD, XD;

  Adder #(.width(32)) adder_1 (.a(ProgramCounter), .b(32'h4), .out(pcplusfour));  // open: cin, cout
  Multiplexer #(.width(32)) multiplexer_1 (.in0(pcplusfour), .in1(adder_2_out), .out(multiplexer_1_out), .sel(PCSel));
  Multiplexer #(.width(32)) multiplexer_2 (
    .in0(multiplexer_1_out), .in1(MemAddress), .out(multiplexer_2_out), .sel(JRSEL));
  Comparator #(.width(7)) comparator_1 (.a(i2[6:0]), .b(7'b1101111), .eq(comparator_1_eq));  // open: gt, lt
  Register #(.width(32)) PC (.D(multiplexer_2_out), .clk(clk), .Q(ProgramCounter));  // open: en, clr
  Comparator #(.width(7)) comparator_2 (.a(i2[6:0]), .b(7'b1100111), .eq(JRSEL));  // open: gt, lt
  or or_1 (or_1_out, comparator_1_eq, JRSEL);
  Multiplexer #(.width(32)) multiplexer_3 (.in0(Instruction), .in1(32'h13), .out(multiplexer_3_out), .sel(flush));
  Adder #(.width(32)) adder_2 (.a(pc2), .b(imm), .out(adder_2_out));  // open: cin, cout
  Register #(.width(32)) register_1 (.D(multiplexer_3_out), .clk(clk), .Q(i2));  // open: en, clr
  Register #(.width(32)) register_2 (.D(ProgramCounter), .clk(clk), .Q(pc2));  // open: en, clr
  or or_2 (flush, PCSel, or_1_out);
  Register #(.width(32)) register_3 (.D(pcplusfour), .clk(clk), .Q(XD));  // open: en, clr
  control_logic control_logic_1 (
    .Instruction(i2), .BrEq(branch_comp_1_breq), .BrLt(branch_comp_1_brlt), .PCSel(PCSel),
    .RegWEn(control_logic_1_regwen), .ImmSel(control_logic_1_immsel), .BrUn(control_logic_1_brun),
    .ASel(control_logic_1_asel), .BSel(control_logic_1_bsel), .ALUSel(control_logic_1_alusel),
    .MemRW(control_logic_1_memrw), .WBSel(control_logic_1_wbsel));
  regfile regfile_1 (
    .ReadIndex1(i2[19:15]), .ReadIndex2(i2[24:20]), .WriteIndex(i2[11:7]), .WriteData(WD),
    .RegWEn(control_logic_1_regwen), .clk(clk), .ra(ra), .sp(sp), .t0(t0), .t1(t1), .t2(t2), .s0(s0),
    .s1(s1), .a0(a0), .ReadData1(regfile_1_readdata1), .ReadData2(rs2));
  imm_gen imm_gen_1 (.Instruction(i2), .ImmSel(control_logic_1_immsel), .Immediate(imm));
  Multiplexer #(.width(32)) multiplexer_4 (.in0(rs2), .in1(imm), .out(multiplexer_4_out), .sel(control_logic_1_bsel));
  Multiplexer #(.width(32)) multiplexer_5 (
    .in0(regfile_1_readdata1), .in1(pc2), .out(multiplexer_5_out), .sel(control_logic_1_asel));
  alu alu_1 (.A(multiplexer_5_out), .B(multiplexer_4_out), .ALUSel(control_logic_1_alusel), .ALUResult(MemAddress));
  branch_comp branch_comp_1 (
    .BrData1(regfile_1_readdata1), .BrData2(rs2), .BrUn(control_logic_1_brun), .BrEq(branch_comp_1_breq),
    .BrLt(branch_comp_1_brlt));
  Adder #(.width(32)) adder_3 (.a(pc2), .b(32'h4));  // open: out, cin, cout
  partial_store partial_store_1 (
    .Instruction(i2), .MemAddress(MemAddress), .DataFromReg(rs2), .MemRW(control_logic_1_memrw),
    .MemWriteMask(MemWriteMask), .DataToMem(MemWriteData));
  partial_load partial_load_1 (
    .Instruction(i2), .MemAddress(MemAddress), .DataFromMem(MemReadData), .DataToReg(partial_load_1_datatoreg));
  Multiplexer #(.select(2), .width(32)) multiplexer_6 (
    .in0(MemAddress), .in1(partial_load_1_datatoreg), .in2(XD), .out(WD), .sel(control_logic_1_wbsel));  // open: in3

  // Other names for the same wires on the sheet: alu_res[31:0] = MemAddress; opcode[6:0] = i2[6:0]

  // Notes on the sheet:
  //   To IMEM
  //   IMEM (do **NOT** move this)
  //   From IMEM
  //   Inputs/Outputs for testing. Do **NOT** move these.
  //   To DMEM
  //   DMEM (do **NOT** move this)
  //   From DMEM
endmodule
