// Logisim project imm-gen.circ as structural Verilog: 1 circuit, main circuit imm_gen
module imm_gen (
  input  [31:0] Instruction,
  input  [2:0] ImmSel,
  output [31:0] Immediate
);

  wire [31:0] bit_extender_1_out, bit_extender_2_out, bit_extender_3_out, bit_extender_4_out,
       bit_extender_5_out, shifter_1_out;

  assign bit_extender_1_out = {{20{Instruction[31]}}, {Instruction[31:25], Instruction[11:7]}};  // Bit_Extender bit_extender_1
  assign bit_extender_2_out = {{20{Instruction[31]}}, {Instruction[31], Instruction[7], Instruction[30:25], Instruction[11:8]}};  // Bit_Extender bit_extender_2
  Shifter #(.width(32)) shifter_1 (.in(bit_extender_2_out), .\dist (5'b00001), .out(shifter_1_out));
  assign bit_extender_3_out = {{20{Instruction[31]}}, Instruction[31:20]};  // Bit_Extender bit_extender_3
  Multiplexer #(.select(3), .width(32)) multiplexer_1 (
    .in0(bit_extender_3_out), .in1(bit_extender_1_out), .in2(shifter_1_out),
    .in3({Instruction[31:12], {12{1'b0}}}), .in4(bit_extender_5_out), .in5(bit_extender_4_out),
    .out(Immediate), .sel(ImmSel));  // open: in6, in7
  assign bit_extender_4_out = {{27{Instruction[19]}}, Instruction[19:15]};  // Bit_Extender bit_extender_4
  assign bit_extender_5_out = {{11{Instruction[31]}}, {Instruction[31], Instruction[19:12], Instruction[20], Instruction[30:21], 1'b0}};  // Bit_Extender bit_extender_5

  // Notes on the sheet:
  //   INPUTS to your circuit
  //   DON'T CHANGE THE LOCATIONS OF THE INPUTS AND OUTPUTS!
  //   OUTPUT from your circuit
endmodule
