// Logisim project partial-load.circ as structural Verilog: 1 circuit, main circuit partial_load
module partial_load (
  input  [31:0] Instruction,
  input  [31:0] MemAddress,
  input  [31:0] DataFromMem,
  output [31:0] DataToReg
);

  wire [7:0] lb;
  wire [15:0] lh;

  Comparator #(.width(3)) comparator_1 (.a(Instruction[14:12]), .b(3'b000));  // open: gt, eq, lt
  Comparator #(.width(3)) comparator_2 (.a(Instruction[14:12]), .b(3'b001));  // open: gt, eq, lt
  Comparator #(.width(3)) comparator_3 (.a(Instruction[14:12]), .b(3'b010));  // open: gt, eq, lt
  Multiplexer #(.select(2), .width(8)) multiplexer_1 (
    .in0(DataFromMem[7:0]), .in1(DataFromMem[15:8]), .in2(DataFromMem[23:16]), .in3(DataFromMem[31:24]),
    .out(lb), .sel(MemAddress[1:0]));
  Multiplexer #(.select(2), .width(16)) multiplexer_2 (
    .in0(DataFromMem[15:0]), .in1(DataFromMem[23:8]), .in2(DataFromMem[31:16]), .out(lh),
    .sel(MemAddress[1:0]));  // open: in3
  Multiplexer #(.select(2), .width(32)) multiplexer_3 (
    .in0({{25{lb[7]}}, lb[6:0]}), .in1({{17{lh[15]}}, lh[14:0]}), .in2(DataFromMem), .out(DataToReg),
    .sel(Instruction[13:12]));  // open: in3

  // Other names for the same wires on the sheet: funct3[2:0] = Instruction[14:12]; lw[31:0] = DataFromMem;
  //   t[1:0] = MemAddress[1:0]

  // Notes on the sheet:
  //   INPUTS to your circuit
  //   DON'T CHANGE THE LOCATIONS OF THE INPUTS AND OUTPUTS!
  //   OUTPUT from your circuit
endmodule
