// Logisim project partial-store.circ as structural Verilog: 1 circuit, main circuit partial_store
module partial_store (
  input  [31:0] Instruction,
  input  [31:0] MemAddress,
  input  [31:0] DataFromReg,
  input  MemRW,
  output [3:0] MemWriteMask,
  output [31:0] DataToMem
);

  wire [3:0] multiplexer_1_out, multiplexer_2_out, multiplexer_5_out;
  wire [7:0] undriven, undriven_2, undriven_3, undriven_4, undriven_5, undriven_6, undriven_7, undriven_8,
       undriven_9, undriven_11, undriven_12, undriven_13;
  wire [15:0] undriven_10, undriven_14;
  wire [31:0] multiplexer_3_out, multiplexer_4_out;

  Multiplexer #(.width(4)) multiplexer_1 (.in0(4'b0011), .in1(4'b1100), .out(multiplexer_1_out), .sel(MemAddress[1]));
  Multiplexer #(.select(2), .width(4)) multiplexer_2 (
    .in0(4'b0001), .in1(4'b0010), .in2(4'b0100), .in3(4'b1000), .out(multiplexer_2_out), .sel(MemAddress[1:0]));
  Multiplexer #(.select(2), .width(32)) multiplexer_3 (
    .in0({undriven_3, undriven_2, undriven, DataFromReg[7:0]}),
    .in1({undriven_6, undriven_5, DataFromReg[7:0], undriven_4}),
    .in2({undriven_9, DataFromReg[7:0], undriven_8, undriven_7}),
    .in3({DataFromReg[7:0], undriven_13, undriven_12, undriven_11}), .out(multiplexer_3_out),
    .sel(MemAddress[1:0]));
  Multiplexer #(.width(32)) multiplexer_4 (
    .in0({undriven_10, DataFromReg[15:0]}), .in1({DataFromReg[15:0], undriven_14}), .out(multiplexer_4_out),
    .sel(MemAddress[1]));
  Multiplexer #(.select(3), .width(4)) multiplexer_5 (
    .in0(multiplexer_2_out), .in1(multiplexer_1_out), .in2(4'b1111), .out(multiplexer_5_out),
    .sel(Instruction[14:12]));  // open: in3, in4, in5, in6, in7
  Multiplexer #(.select(3), .width(32)) multiplexer_6 (
    .in0(multiplexer_3_out), .in1(multiplexer_4_out), .in2(DataFromReg), .out(DataToMem),
    .sel(Instruction[14:12]));  // open: in3, in4, in5, in6, in7
  assign MemWriteMask = {4{MemRW}} & multiplexer_5_out;  // AND_Gate and_1, 4 bits wide

  // Other names for the same wires on the sheet: sb[7:0] = DataFromReg[7:0]; sh[15:0] = DataFromReg[15:0];
  //   sw[31:0] = DataFromReg; opcode[6:0] = Instruction[6:0]; funct3[2:0] = Instruction[14:12];
  //   t[1:0] = MemAddress[1:0]

  // Notes on the sheet:
  //   INPUTS to your circuit
  //   DON'T CHANGE THE LOCATIONS OF THE INPUTS AND OUTPUTS!
  //   OUTPUT from your circuit
endmodule
